// Logisim project Easy.circ as structural Verilog: 1 circuit, main circuit main
module main (
  input  in_1,
  input  in_2,
  input  in_3,
  input  in_4,
  input  in_5,
  input  in_6,
  input  in_7,
  input  in_8,
  input  in_9,
  input  in_10,
  input  in_11,
  input  in_12,
  input  in_13,
  input  in_14,
  input  in_15,
  input  in_16,
  input  in_17,
  input  in_18,
  input  in_19,
  input  in_20,
  input  in_21,
  input  in_22,
  input  in_23,
  input  in_24,
  input  in_25,
  input  in_26,
  output out_27,
  output out_28,
  output out_29,
  output out_30,
  output out_31,
  output out_32,
  output out_33,
  output out_34,
  output out_35,
  output out_36
);

  wire button_1_out, button_2_out, nand_2_out, nand_3_out, nand_4_out, nand_6_out, nor_2_out, nor_4_out,
       nor_6_out, nor_8_out, xnor_2_out;

  not not_1 (out_27, in_2);
  or or_1 (out_29, in_4, in_6);
  nor nor_1 (out_32, in_9, in_12);
  xnor xnor_1 (out_34, in_16, in_18);
  and and_1 (out_28, in_1, in_3);
  nand nand_1 (out_30, in_5, in_7);
  xor xor_1 (out_33, in_10, in_13);
  Button button_1 (.out(button_1_out));
  Button button_2 (.out(button_2_out));
  nand nand_2 (nand_2_out, in_8, in_11);
  nand nand_3 (nand_3_out, in_14, in_15);
  nor nor_2 (nor_2_out, in_17, in_19);
  LED led_1 (.in(button_1_out));
  LED led_2 (.in(button_2_out));
  LED led_3 (.in(button_2_out));
  nand nand_4 (nand_4_out, nand_2_out, nand_2_out);
  nand nand_5 (nand_4_out, nand_3_out, nand_3_out);
  nor nor_3 (in_20, nor_2_out, nor_2_out);
  NotExactlyOne xnor_2 (.out(xnor_2_out), .in0(in_23), .in1(in_24), .in2(in_25), .in4(in_26));
  not nand_6 (nand_6_out, nand_4_out);  // NAND_Gate
  not nor_4 (nor_4_out, in_20);  // NOR_Gate
  nand nand_7 (out_31, nand_6_out, nand_6_out);
  nor nor_5 (in_21, nor_4_out, nor_4_out);
  xnor xnor_3 (out_36, xnor_2_out, 1'b0);
  not nor_6 (nor_6_out, in_21);  // NOR_Gate
  nor nor_7 (in_22, nor_6_out, nor_6_out);
  not nor_8 (nor_8_out, in_22);  // NOR_Gate
  nor nor_9 (out_35, nor_8_out, nor_8_out);

  // Notes on the sheet:
  //   Easy
  //   Basic Logic Gates
  //   LED Control Circuits
  //   Advanced Logic Gate Implementations
endmodule
