// Logisim project M910.circ as structural Verilog: 2 circuits, main circuit Multiplexers
module Multiplexers (
  input  a,
  input  A_2,
  input  B,
  input  a_3,
  input  b_2,
  input  A_4,
  input  B_3,
  input  C,
  input  D,
  output F,
  output F_2
);

  wire and_1_out, and_2_out, and_3_out, and_4_out, and_5_out, and_6_out;

  and and_1 (and_1_out, ~a, A_2);  // AND_Gate
  and and_2 (and_2_out, a, B);
  or or_1 (F, and_1_out, and_2_out);
  and and_3 (and_3_out, ~b_2, ~a_3, A_4);  // AND_Gate
  and and_4 (and_4_out, ~a_3, b_2, B_3);  // AND_Gate
  and and_5 (and_5_out, a_3, ~b_2, C);  // AND_Gate
  and and_6 (and_6_out, b_2, a_3, D);
  or or_2 (F_2, and_3_out, and_4_out, and_5_out, and_6_out);

  // Notes on the sheet:
  //   Select
  //   Select
  //   2-input Multiplexer
  //   4-input Multiplexer
endmodule

module Demultiplexers (
  input  a,
  input  A_2,
  input  a_3,
  input  b,
  input  A_4,
  output F1,
  output F2,
  output F1_2,
  output F2_2,
  output F3,
  output F4
);

  and and_1 (F1, ~a, A_2);  // AND_Gate
  and and_2 (F2, a, A_2);
  and and_3 (F1_2, ~b, ~a_3, A_4);  // AND_Gate
  and and_4 (F2_2, ~a_3, b, A_4);  // AND_Gate
  and and_5 (F3, a_3, ~b, A_4);  // AND_Gate
  and and_6 (F4, b, a_3, A_4);

  // Notes on the sheet:
  //   Select
  //   Select
  //   2-output Demultiplexer
  //   4-output Multiplexer
endmodule
