// Logisim project Meduim.circ as structural Verilog: 1 circuit, main circuit main
// S
module main (
  input  J,
  input  S,
  input  R,
  input  K,
  input  D,
  input  in_6,
  output out_7,
  output Q,
  output Q_prime,
  output out_10,
  output out_11,
  output out_12,
  output out_13,
  output out_14
);

  wire and_1_out, and_2_out, and_3_out, and_4_out, and_5_out, and_6_out, clock_1_out, clock_2_out,
       clock_3_out, clock_4_out, nand_1_out, nand_2_out, not_1_out;

  Clock clock_1 (.out(clock_1_out));
  and and_1 (and_1_out, S, clock_1_out);
  and and_2 (and_2_out, clock_1_out, R);
  not not_1 (not_1_out, D);
  Clock clock_2 (.out(clock_2_out));
  nor nor_1 (Q, and_1_out, Q_prime);
  nor nor_2 (Q_prime, Q, and_2_out);
  nand nand_1 (nand_1_out, D, clock_2_out);
  nand nand_2 (nand_2_out, not_1_out, clock_2_out);
  nand nand_3 (out_11, nand_1_out, out_12);
  nand nand_4 (out_12, out_11, nand_2_out);
  Clock clock_3 (.out(clock_3_out));
  Clock clock_4 (.out(clock_4_out));
  and and_3 (and_3_out, out_7, J, clock_4_out);
  and and_4 (and_4_out, clock_4_out, K, out_10);
  and and_5 (and_5_out, in_6, clock_3_out);
  and and_6 (and_6_out, clock_3_out, in_6);
  nor nor_3 (out_7, and_3_out, out_10);
  nor nor_4 (out_10, out_7, and_4_out);
  nor nor_5 (out_13, and_5_out, out_14);
  nor nor_6 (out_14, out_13, and_6_out);

  // Notes on the sheet:
  //   Meduim:
  //   SR Flip-Flop
  //   D Flip-Flop
  //   J-K Flip-Flop
  //   T flip-flop:
endmodule
