// Logisim project lab5.circ as structural Verilog: 1 circuit, main circuit main
module main (
  input  _1,
  input  in_2,
  input  in_3,
  input  in_4,
  input  in_5,
  output out_6,
  output out_7
);

  wire and_3_out, clock_1_out, nand_1_out, nand_2_out, nand_3_out, nand_4_out, nor_1_out, not_1_out,
       not_2_out, undriven, undriven_2, undriven_3, undriven_4;

  Clock clock_1 (.out(clock_1_out));
  // AND_Gate and_1 has open pins: in0=_1, in4=clock_1_out, out=open
  // AND_Gate and_2 has open pins: in1=clock_1_out, in4=in_3, out=open
  not not_1 (not_1_out, undriven);
  nand nand_1 (nand_1_out, undriven, undriven_2);
  nand nand_2 (nand_2_out, undriven_2, not_1_out);
  nor nor_1 (nor_1_out, undriven_4, out_7);
  // NOR_Gate nor_2 has open pins: in1=out_6, in3=undriven_3, out=open
  nand nand_3 (nand_3_out, nand_1_out, nand_4_out);
  nand nand_4 (nand_4_out, nand_3_out, nand_2_out);
  LED led_1 (.in(not_2_out));
  not not_2 (not_2_out, in_2);
  and and_3 (and_3_out, in_4, in_5);
  LED led_2 (.in(and_3_out));

  // Notes on the sheet:
  //   2)
  //   5)
  //   7)
  //   9)
  //   10)
  //   Meduim:
  //   3)
  //   4)
  //   6)
  //   8)
  //   Easy:
  //   1)
  //   2)
endmodule
